// Logisim project t3lc.circ as structural Verilog: 4 circuits, main circuit test_t3lc
module alu (
  input  [7:0] A,
  input  [7:0] B,
  input  [2:0] OP,
  input  ENA,
  output [7:0] RES
);

  wire comparator_1_eq, comparator_1_gt;
  wire [7:0] adder_1_out, and_1_out, bit_extender_1_out, bit_extender_2_out, multiplier_1_out, not_1_out,
       or_1_out, shifter_1_out;

  Adder adder_1 (.a(A), .b(B), .out(adder_1_out));  // open: cin, cout
  assign and_1_out = A & B;  // AND_Gate and_1, 8 bits wide
  assign or_1_out = A | B;  // OR_Gate or_1, 8 bits wide
  assign not_1_out = ~A;  // NOT_Gate not_1, 8 bits wide
  Shifter shifter_1 (.in(A), .\dist (B[2:0]), .out(shifter_1_out));
  Multiplier multiplier_1 (.a(A), .b(B), .out(multiplier_1_out));  // open: cin, cout
  Comparator comparator_1 (.a(A), .b(B), .gt(comparator_1_gt), .eq(comparator_1_eq));  // open: lt
  assign bit_extender_1_out = {{7{1'b0}}, comparator_1_gt};  // Bit_Extender bit_extender_1
  assign bit_extender_2_out = {{7{1'b0}}, comparator_1_eq};  // Bit_Extender bit_extender_2
  Multiplexer #(.disabled("Z"), .enable("true"), .select(3), .width(8)) multiplexer_1 (
    .in0(adder_1_out), .in1(and_1_out), .in2(or_1_out), .in3(not_1_out), .in4(shifter_1_out),
    .in5(multiplier_1_out), .in6(bit_extender_1_out), .in7(bit_extender_2_out), .out(RES), .sel(OP), .en(ENA));
endmodule

module stack (
  input  WRITE_SP,
  input  PUSH,
  input  POP,
  input  TOS,
  input  CLK,
  input  RESET,
  output [7:0] DATA
);

  wire or_1_out, or_2_out;
  wire [7:0] CNT_SP_q, multiplexer_1_out, subtractor_1_out;

  or or_1 (or_1_out, PUSH, POP);
  or or_2 (or_2_out, POP, TOS);
  Counter CNT_SP (
    .load(WRITE_SP), .D(DATA), .count(or_1_out), .Q(CNT_SP_q), .up(PUSH), .clk(CLK), .clr(RESET));  // open: carry
  Subtractor subtractor_1 (.a(CNT_SP_q), .b(8'h1), .out(subtractor_1_out));  // open: bin, bout
  Multiplexer #(.width(8)) multiplexer_1 (.in0(subtractor_1_out), .in1(CNT_SP_q), .out(multiplexer_1_out), .sel(PUSH));
  RAM #(.clearpin("true"), .databus("bidir")) ram_1 (
    .addr(multiplexer_1_out), .we(PUSH), .oe(or_2_out), .clk(CLK), .data(DATA), .clr(RESET));
endmodule

module t3lc (
  input  [7:0] ROM_VALUE,
  input  CLK,
  input  RESET,
  input  RUN,
  output RAM_READ,
  output RAM_WRITE,
  output [7:0] DATA,
  output [15:0] RAM_ADDR,
  output [15:0] ROM_ADDR
);

  wire decoder_1_out0, decoder_1_out1, decoder_1_out2, decoder_1_out3, decoder_1_out4, decoder_1_out5,
       decoder_1_out6, decoder_2_out0, decoder_2_out1, decoder_2_out2, decoder_2_out3, decoder_2_out4,
       decoder_2_out5, decoder_2_out6, decoder_2_out8, decoder_2_out9, not_1_out, or_1_out;
  wire [7:0] bit_extender_1_out, decoder_2_out10, REG_A_q, REG_B_q, REG_IMM_q;

  not not_1 (not_1_out, ROM_VALUE[7]);
  assign bit_extender_1_out = {{1{1'b0}}, ROM_VALUE[6:0]};  // Bit_Extender bit_extender_1
  Decoder #(.select(3)) decoder_1 (
    .out0(decoder_1_out0), .out1(decoder_1_out1), .out2(decoder_1_out2), .out3(decoder_1_out3),
    .out4(decoder_1_out4), .out5(decoder_1_out5), .out6(decoder_1_out6), .out7(RAM_WRITE),
    .sel(ROM_VALUE[6:4]), .en(not_1_out));
  Register REG_IMM (.D(bit_extender_1_out), .en(ROM_VALUE[7]), .clk(CLK), .Q(REG_IMM_q), .clr(RESET));
  Register REG_A (.D(DATA), .en(decoder_1_out0), .clk(CLK), .Q(REG_A_q), .clr(RESET));
  Register REG_B (.D(DATA), .en(decoder_1_out1), .clk(CLK), .Q(REG_B_q), .clr(RESET));
  Register REG_I (.D(DATA), .en(decoder_1_out2), .clk(CLK), .Q(RAM_ADDR[7:0]), .clr(RESET));
  Register REG_J (.D(DATA), .en(decoder_1_out3), .clk(CLK), .Q(RAM_ADDR[15:8]), .clr(RESET));
  assign DATA = decoder_2_out0 ? REG_A_q : 8'bz;  // Controlled_Buffer controlled_buffer_1
  assign DATA = decoder_2_out1 ? REG_B_q : 8'bz;  // Controlled_Buffer controlled_buffer_2
  assign DATA = decoder_2_out2 ? RAM_ADDR[7:0] : 8'bz;  // Controlled_Buffer controlled_buffer_3
  assign DATA = decoder_2_out3 ? RAM_ADDR[15:8] : 8'bz;  // Controlled_Buffer controlled_buffer_4
  Decoder #(.select(4)) decoder_2 (
    .out0(decoder_2_out0), .out1(decoder_2_out1), .out2(decoder_2_out2), .out3(decoder_2_out3),
    .out4(decoder_2_out4), .out5(decoder_2_out5), .out6(decoder_2_out6), .out7(RAM_READ),
    .out8(decoder_2_out8), .out9(decoder_2_out9), .out10(decoder_2_out10[0]), .out11(decoder_2_out10[1]),
    .out12(decoder_2_out10[2]), .out13(decoder_2_out10[3]), .out14(decoder_2_out10[4]),
    .out15(decoder_2_out10[7]), .sel(ROM_VALUE[3:0]), .en(not_1_out));
  assign DATA = decoder_2_out8 ? REG_IMM_q : 8'bz;  // Controlled_Buffer controlled_buffer_5
  Counter #(.max('hffff), .width(16)) PC (
    .load(decoder_1_out4), .D(RAM_ADDR), .count(RUN), .Q(ROM_ADDR), .clk(CLK), .clr(RESET));  // open: carry, up
  assign DATA = decoder_2_out9 ? {8{1'b0}} : 8'bz;  // Controlled_Buffer controlled_buffer_6
  or or_1 (or_1_out, decoder_2_out10[0], decoder_2_out10[1], decoder_2_out10[2], decoder_2_out10[3], decoder_2_out10[4], decoder_2_out10[7]);
  alu alu_1 (.A(REG_A_q), .B(REG_B_q), .OP(RAM_ADDR[6:4]), .ENA(decoder_2_out6), .RES(DATA));
  stack stack_1 (
    .WRITE_SP(decoder_1_out6), .PUSH(decoder_1_out5), .POP(decoder_2_out4), .TOS(decoder_2_out5), .CLK(CLK),
    .RESET(RESET), .DATA(DATA));
  assign DATA = or_1_out ? {decoder_2_out10[7], 2'b00, decoder_2_out10[4:0]} : 8'bz;  // Controlled_Buffer controlled_buffer_7
endmodule

module test_t3lc (
  input  RESET,
  input  RUN
);

  wire and_1_out, and_2_out, CLK_out, comparator_1_eq, not_1_out, t3lc_1_ram_read, t3lc_1_ram_write;
  wire [6:0] t3lc_1_data;
  wire [7:0] rom_1_data;
  wire [7:7] t3lc_1_data_2;
  wire [15:0] t3lc_1_ram_addr, t3lc_1_rom_addr;

  Clock CLK (.out(CLK_out));
  ROM #(.addrWidth(16)) rom_1 (.addr(t3lc_1_rom_addr), .data(rom_1_data));
  t3lc t3lc_1 (
    .ROM_VALUE(rom_1_data), .CLK(CLK_out), .RESET(RESET), .RUN(RUN), .RAM_ADDR(t3lc_1_ram_addr),
    .ROM_ADDR(t3lc_1_rom_addr), .RAM_READ(t3lc_1_ram_read), .DATA({t3lc_1_data_2[7], t3lc_1_data}),
    .RAM_WRITE(t3lc_1_ram_write));
  RAM #(.addrWidth(16), .clearpin("true"), .databus("bidir")) ram_1 (
    .addr(t3lc_1_ram_addr), .we(t3lc_1_ram_write), .oe(and_1_out), .clk(CLK_out),
    .data({t3lc_1_data_2[7], t3lc_1_data}), .clr(RESET));
  and and_1 (and_1_out, t3lc_1_ram_read, not_1_out);
  and and_2 (and_2_out, t3lc_1_ram_read, comparator_1_eq);
  Comparator #(.width(16)) comparator_1 (.a(t3lc_1_ram_addr), .b(16'h7f7f), .eq(comparator_1_eq));  // open: gt, lt
  not not_1 (not_1_out, comparator_1_eq);
  TTY tty_1 (.data(t3lc_1_data), .clk(CLK_out), .we(and_2_out), .clr(RESET));

  // Notes on the sheet:
  //   contents of rom_1 (hex, n*v repeats v):
  //   c8 58 e5 58 ec 58 ec 58 ef 58 8a 58 ff 28 ff 38 5*74
endmodule
